# Fritzing sketch Full Schematic Circuit of the Robot (saved by Fritzing 0.9.3b)
perfboards: 1

parts:
  Buck_Convertor1 = Buck Convertor [part_number=LM2596 package=THT]
  8_V_output = Buck Convertor [part_number=LM2596 package=THT]
  J1 = Camdenboss CTB0158-2 [part_number=CTB0158-2 package=THT]
  U2 = LIPO-2000mAh [package=lipo-2000]  # not connected
  U2_2 = LIPO-2000mAh [package=lipo-2000]  # not connected
  U2_3 = LIPO-2000mAh [package=lipo-2000]  # not connected
  Part1 = LIPO-2200mAh
  Part2 = LIPO-2200mAh
  Part3 = LIPO-2200mAh
  J2 = Camdenboss CTB0158-2 [part_number=CTB0158-2 package=THT]
  J3 = Camdenboss CTB0158-2 [part_number=CTB0158-2 package=THT]
  J4 = Camdenboss CTB0158-2 [part_number=CTB0158-2 package=THT]
  J5 = Camdenboss CTB0158-2 [part_number=CTB0158-2 package=THT]
  6_5_V_output = Buck Convertor [part_number=LM2596 package=THT]
  J6 = single row smd male pin header, 10 pins [form="♂ (male)"]
  J7 = single row smd male pin header, 10 pins [form="♂ (male)"]
  J8 = single row smd male pin header, 10 pins [form="♂ (male)"]
  J9 = single row smd male pin header, 10 pins [form="♂ (male)"]
  J10 = Camdenboss CTB0158-2 [part_number=CTB0158-2 package=THT]
  J11 = XL4015 DC-DC CC CV module (blue)
  M1 = DC Motor
  J12 = Basic Servo
  Part4 = Arduino Mega 2560 (Rev3)
  Part5 = SRF05 Ultrasonic Rangefinder
  Part6 = SRF05 Ultrasonic Rangefinder
  Part7 = SRF05 Ultrasonic Rangefinder
  Part8 = SRF05 Ultrasonic Rangefinder
  Part9 = SRF05 Ultrasonic Rangefinder
  Part10 = SRF05 Ultrasonic Rangefinder
  Part11 = SRF05 Ultrasonic Rangefinder
  J13 = Basic Servo
  J14 = Basic Servo
  J15 = Basic Servo
  A2 = drv-1012
  A1 = Raspberry Pi 5
  U3 = TCM8240MD [package=tcm8240md]

nets:
  N1: Buck_Convertor1.Negative_Output, J5.pin1
  N2: Buck_Convertor1.Positive_Output, J5.pin2
  N3: 8_V_output.Negative_Output, J3.pin1
  N4: J1.pin1, J4.pin2
  N5: J1.pin2, 6_5_V_output.Negative_Input
  N6: J1.terminal_1, Part3.+
  N7: J1.terminal_2, Part1.-
  N8: Part1.+, Part2.-
  N9: Part2.+, Part3.-
  N10: J2.pin1, 6_5_V_output.Negative_Output
  N11: J2.pin2, 6_5_V_output.Positive_Output
  N12: J2.terminal_1, J12.gnd
  N13: J2.terminal_2, J12.vcc
  N14: J3.terminal_1, Part4.GND
  N15: J4.terminal_1, J11.pin_1
  N16: J4.terminal_2, J11.pin_2
  N17: J5.terminal_1, J15.gnd
  N18: J5.terminal_2, J15.vcc, A2.Pin_5
  N19: J6.pin1, J7.pin1, Part9.GND
  N20: J6.pin2, J7.pin2
  N21: J6.pin3, J7.pin3
  N22: J6.pin4, J7.pin4
  N23: J6.pin5, J7.pin5
  N24: J6.pin6, J7.pin6
  N25: J6.pin7, J7.pin7
  N26: J6.pin8, J7.pin8
  N27: J6.pin9, J7.pin9
  N28: J6.pin10, J7.pin10
  N29: J8.pin2, J9.pin2
  N30: J8.pin3, J9.pin3
  N31: J8.pin4, J9.pin4
  N32: J8.pin5, J9.pin5
  N33: J8.pin6, J9.pin6
  N34: J8.pin7, J9.pin7
  N35: J8.pin8, J9.pin8
  N36: J8.pin9, J9.pin9
  N37: J8.pin10, J9.pin10
  N38: J10.terminal_1, A2.Pin_11
  N39: J10.terminal_2, A2.Pin_12
  N40: M1.pin_1, A2.Pin_10
  N41: M1.pin_2, A2.Pin_9
  N42: J12.pulse, Part4.D8_PWM
  N43: Part4.D0_RX0, A1.GPIO14
  N44: Part4.D1_TX0, A1.GPIO15
  N45: Part4.D3_PWM, A2.Pin_4
  N46: Part4.D4_PWM, A2.Pin_8
  N47: Part4.D5_PWM, J13.pulse
  N48: Part4.D6_PWM, J14.pulse
  N49: Part4.D7_PWM, J15.pulse
  N50: Part4.D40, Part5.Echo
  N51: Part4.D42, Part6.Echo
  N52: Part4.D44, Part7.Echo
  N53: Part4.D46, Part11.Echo
  N54: Part4.D48, Part9.Echo
  N55: Part4.D50, Part10.Echo
  N56: Part4.D52, Part8.Echo
  N57: U3.EXTCLK, U3.DOUT4

notes:
  6.5 V Output
  8 V Output
  5 V Output
  5 V Output (High Current)
  RaspberryPi 5
  DC JGA25-370 245 RPM
  Mg996R Servo Motor
  3 SG90 Servo Motors
  7 HC-04 UltraSonic Sensor
  Input
  BTS7960 Motor Driver
  Arducam 64Mp Hawk-Eye Auto Focus

custom parts:
  Buck Convertor: DC to DC buck convertor
  LIPO-2200mAh: 2200mAh Lipo-battery
  XL4015 DC-DC CC CV module (blue): XL4015 DC-DC CC/CV module blue
  drv-1012: .The BTS7960 is a fully integrated high current H bridge module for motor drive applications.
  Raspberry Pi 5: The RPi5, a faster version of the awesome Raspberry Pi4B ARM Board with 40 pin gpio.
